# Fritzing sketch ShockCell (saved by Fritzing 0.9.4)
breadboards: 1

parts:
  Microcontroller = ESP32S-HiLetgo [part_number=ESP32S]
  Motor_for_Lock = Basic Servo
  Safe_door_opening_sensor = Round Pushbutton
  Shock_button_of_remote_control = SWITCH-MOMENTARY-2 [package=reed_switch_plastic]
  Transistor = TRANSISTOR_NPN [part_number=BC547 package=to-92-ammo]
  Resistor = Resistor [tolerance=±5% resistance=10k package=THT]

nets (from the schematic view):
  N1: Microcontroller.GND, Safe_door_opening_sensor.leg1, Shock_button_of_remote_control.2, Transistor.E
  N2: Microcontroller.GPIO15, Safe_door_opening_sensor.leg0
  N3: Microcontroller.GPIO2, Motor_for_Lock.pulse
  N4: Microcontroller.GPIO4, Resistor.Pin_1
  N5: Shock_button_of_remote_control.1, Transistor.C
  N6: Transistor.B, Resistor.Pin_0

notes:
  Wi-Fi parameters
  - SSID
  - WLAN password
  Telegram bot
  Chastikey
  IFTTT
  Button of shock
  collar remote
  Motor opening
  the safe lock
  Safe door
  opening
  sensor

custom parts:
  ESP32S-HiLetgo: HiLetgo ESP-WROOM-32 ESP32 ESP-32S Development Board 2.4GHz Dual-Mode WiFi + Bluetooth Dual Cores Microcontroller The ESP32 integrated with Antenna switches, RF Balun, power amplifiers, low-noise amplifiers, filters, and management modules, and the entire solution occupies the least area of PCB. 2.4 GHz Wi-Fi plus Bluetooth dual-mode chip, with TSMC Ultra-low power consumption 40nm technology,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
